# Fritzing sketch raspi-door (saved by Fritzing 0.9.6b)
breadboards: 1

parts:
  Raspberry_Pi_1 = Raspberry Pi 3 [part_number=RPI-3-V1.2]
  LED1 = LED - 5mm [color="Red (633nm)" current=0.030 package="5 mm [THT]"]
  S1 = Pushbutton [package="[THT]"]
  R2 = Resistor [tolerance=±5% power=0.25 resistance=10k package=THT]
  R1_-_330 = Resistor [tolerance=±5% power=0.25 resistance=330 package=THT]

nets:
  N1: Raspberry_Pi_1.3v3, R2.Pin_1
  N2: Raspberry_Pi_1.GPIO24, S1.Pin_3, S1.Pin_4
  N3: Raspberry_Pi_1.GPIO23, R1_-_330.Pin_1
  N4: Raspberry_Pi_1.GND, LED1.cathode
  N5: LED1.anode, R1_-_330.Pin_0
  N6: S1.Pin_1, S1.Pin_2, R2.Pin_0
