# Fritzing sketch raspidoor (saved by Fritzing 0.9.6b)
breadboards: 1

parts:
  Raspberry_Pi_1 = Raspberry Pi 3 [part_number=RPI-3-V1.2]
  LED1 = LED - 5mm [color="Red (633nm)" current=0.030 package="5 mm [THT]"]
  S1 = Pushbutton [package="[THT]"]
  R1_-_330 = Resistor [tolerance=±5% power=0.25 resistance=150 package=THT]
  Power_plug1 = Power plug
  R2 = Resistor [tolerance=±5% power=0.25 resistance=10k package=THT]
  S2 = Pushbutton [package="[THT]"]
  R4 = Resistor [tolerance=±5% power=0.25 resistance=10k package=THT]
  J1 = Piezo Speaker
  Mod1 = KY-019 5V Relay Module [package="Breakout board"]

nets:
  N1: Raspberry_Pi_1.GND, LED1.cathode, S1.Pin_1, S1.Pin_2, S2.Pin_1, S2.Pin_2, Mod1.-
  N2: Raspberry_Pi_1.GPIO25, Mod1.S
  N3: Raspberry_Pi_1.GPIO24, S2.Pin_3, S2.Pin_4, R4.Pin_0
  N4: Raspberry_Pi_1.GPIO23, S1.Pin_3, S1.Pin_4, R2.Pin_0
  N5: Raspberry_Pi_1.GPIO18, R1_-_330.Pin_1
  N6: Raspberry_Pi_1.5V, R2.Pin_1, R4.Pin_1, Mod1.+
  N7: LED1.anode, R1_-_330.Pin_0
  N8: Power_plug1.GND, J1.pin2
  N9: Power_plug1.VCC, Mod1.NO
  N10: J1.pin1, Mod1.Common

custom parts:
  KY-019 5V Relay Module: KY-019 5V Relay module, used to control AC circuits. (Special thanks to vanepp for fixing the PCB holes and other errors)
